// Logisim project circuitoexercicio.circ as structural Verilog: 2 circuits, main circuit main
module main (
  input  A,
  input  B,
  input  C,
  output out_4
);

  EXE_1 exe_1_1 (.A(A), .B(B), .C(C), .S(out_4));
endmodule

module EXE_1 (
  input  A,
  input  B,
  input  C,
  output S
);

  wire and_1_out, not_1_out, not_2_out, not_3_out, or_1_out, xor_1_out;

  xor xor_1 (xor_1_out, A, B);
  not not_1 (not_1_out, B);
  or or_1 (or_1_out, xor_1_out, not_1_out);
  not not_2 (not_2_out, A);
  and and_1 (and_1_out, not_2_out, or_1_out);
  not not_3 (not_3_out, C);
  or or_2 (S, and_1_out, not_3_out);
endmodule
